// Logisim project processor.circ as structural Verilog: 12 circuits, main circuit main
module main (
  input  [7:0] in_1,
  input  [7:0] in_2,
  input  [7:0] in_3,
  input  [7:0] in_4,
  output [24:0] out_5,
  output [7:0] out_6,
  output [4:0] out_7,
  output [7:0] out_8,
  output [7:0] out_9,
  output [7:0] out_10,
  output [7:0] out_11,
  output [2:0] out_12
);

  wire ALU_Save, C_Save, Carry_Flag, Carry_Flag_D1, Carry_Flag_D2, clk, comparator_1_eq, INPort_R, not_1_out,
       not_2_out, not_3_out, OUTPort_W, Reg_R, Reg_W, SRAM_R, SRAM_W, Stack_R, Stack_W, T0, T0_I0, T0_I1,
       T0_I2, T0_I3, T0_I4, T1, T1_I0, T1_I1, T1_I2, T1_I3, T1_I4, T2, T2_I0, T2_I1, T2_I2, T2_I3, T2_I4, T3,
       T3_I0, T3_I1, T3_I2, T3_I3, T3_I4, T4, T4_I0, T4_I1, T4_I2, T4_I3, T4_I4, UpdatePC, Z_Save, Zero_Flag,
       Zero_Flag_D1, Zero_Flag_D2;
  wire [2:0] adder_1_out, multiplexer_2_out;
  wire [3:0] x, x_D1, x_D2, x_D3, y, y_D1, y_D2, y_D3, z, z_D1, z_D2, z_D3;
  wire [4:0] OPCODE_D1, OPCODE_D2, OPCODE_D3;
  wire [7:0] ALUOut, ALUOut_D1, Dout_INPort, Dout_SRAM, Dout_Stack, Imm, Imm_D1, Imm_D2, Imm_D3,
       multiplexer_1_out, multiplexer_7_out, multiplexer_10_out, multiplexer_11_out, multiplexer_12_out,
       PC_D2, Rx, Rx_D1, Rx_D2, Ry, Ry_D1, Ry_D2;

  Clock clock_1 (.out(clk));
  Adder #(.width(3)) adder_1 (.a(out_12), .b(3'b001), .out(adder_1_out), .cin(1'b0));  // open: cout
  Multiplexer #(.select(5), .width(8), .enable("false")) multiplexer_1 (
    .in13(Imm_D3), .in14(Imm_D3), .in15(Imm_D3), .in16(Imm_D3), .in17(Imm_D3), .in27(ALUOut_D1),
    .in28(ALUOut_D1), .out(multiplexer_1_out), .sel(OPCODE_D3));  // open: in0, in1, in2, in3, in4, in5, in6, in7, in8, in9, in10, in11, in12, in18, in19, in20, in21, in22, in23, in24, in25, in26, in29, in30, in31
  Timing timing_1 (.clk(clk), .T0(T0_I0), .T1(T1_I0), .T2(T2_I0), .T3(T3_I0), .T4(T4_I0));
  Timing timing_2 (.clk(clk), .T0(T3_I2), .T1(T4_I2), .T2(T0_I2), .T3(T1_I2), .T4(T2_I2));
  Multiplexer #(.width(3), .enable("false")) multiplexer_2 (
    .in0(adder_1_out), .in1(3'b000), .out(multiplexer_2_out), .sel(comparator_1_eq));
  Comparator #(.width(3)) comparator_1 (.a(3'b100), .b(out_12), .eq(comparator_1_eq));  // open: gt, lt
  PC pc_1 (
    .EnablePC(T0), .clk(clk), .UpdatePC(UpdatePC), .NewCAddress(multiplexer_1_out), .PC(out_6), .PC_D2(PC_D2));  // open: PC_D1
  Register #(.width(3)) register_1 (.D(multiplexer_2_out), .en(1'b1), .Q(out_12), .clk(clk), .clr(1'b0));
  Timing timing_3 (.clk(clk), .T0(T1_I4), .T1(T2_I4), .T2(T3_I4), .T3(T4_I4), .T4(T0_I4));
  Timing timing_4 (.clk(clk), .T0(T4_I1), .T1(T0_I1), .T2(T1_I1), .T3(T2_I1), .T4(T3_I1));
  Multiplexer #(.select(3), .enable("false")) multiplexer_3 (
    .in0(T0_I0), .in1(T0_I1), .in2(T0_I2), .in3(T0_I3), .in4(T0_I4), .out(T0), .sel(out_12));  // open: in5, in6, in7
  Multiplexer #(.select(3), .enable("false")) multiplexer_4 (
    .in0(T2_I3), .in1(T2_I4), .in2(T2_I0), .in3(T2_I1), .in4(T2_I2), .out(T2), .sel(out_12));  // open: in5, in6, in7
  ROM_SynR rom_synr_1 (
    .Address(out_6), .clk(clk), .R(T0), .Inst(out_5), .Imm(Imm), .Source2(y), .Source1(x), .Dest(z),
    .OPCODE(out_7), .Imm_D1(Imm_D1), .Source2_D1(y_D1), .Source1_D1(x_D1), .Dest_D1(z_D1),
    .OPCODE_D1(OPCODE_D1), .Imm_D2(Imm_D2), .Source2_D2(y_D2), .Source1_D2(x_D2), .Dest_D2(z_D2),
    .OPCODE_D2(OPCODE_D2), .Imm_D3(Imm_D3), .Source2_D3(y_D3), .Source1_D3(x_D3), .Dest_D3(z_D3),
    .OPCODE_D3(OPCODE_D3));  // open: Inst_D1, Inst_D2, Inst_D3
  OUTPort outport_1 (
    .DatainOUTPort(ALUOut), .clk(clk), .W(OUTPort_W), .CurrentAddress(Imm_D2),
    .DatavisibletoExternal1World(out_8), .DatavisibletoExternal2World(out_9),
    .DatavisibletoExternal3World(out_10), .DatavisibletoExternal4World(out_11));
  Timing timing_5 (.clk(clk), .T0(T2_I3), .T1(T3_I3), .T2(T4_I3), .T3(T0_I3), .T4(T1_I3));
  Multiplexer #(.select(3), .enable("false")) multiplexer_5 (
    .in0(T1_I4), .in1(T1_I0), .in2(T1_I1), .in3(T1_I2), .in4(T1_I3), .out(T1), .sel(out_12));  // open: in5, in6, in7
  Multiplexer #(.select(3), .enable("false")) multiplexer_6 (
    .in0(T3_I2), .in1(T3_I3), .in2(T3_I4), .in3(T3_I0), .in4(T3_I1), .out(T3), .sel(out_12));  // open: in5, in6, in7
  INPort inport_1 (
    .DatacomingfromExternal1World(in_1), .clk(clk), .DatacomingfromExternal2World(in_2),
    .DatacomingfromExternal3World(in_3), .DatacomingfromExternal4World(in_4), .CurrentAddress(Imm_D2),
    .R(INPort_R), .INPort2Dout(Dout_INPort));  // open: INPort1Dout, INPortDataout, INPort3Dout, INPort4Dout
  Multiplexer #(.select(5), .width(8), .enable("false")) multiplexer_7 (
    .in1(ALUOut_D1), .in2(ALUOut_D1), .in3(ALUOut_D1), .in4(ALUOut_D1), .in5(ALUOut_D1), .in6(ALUOut_D1),
    .in7(ALUOut_D1), .in8(ALUOut_D1), .in9(ALUOut_D1), .in10(ALUOut_D1), .in11(Dout_SRAM), .in19(Dout_Stack),
    .in20(Dout_INPort), .in22(Dout_SRAM), .in24(ALUOut_D1), .in25(ALUOut_D1), .in26(ALUOut_D1),
    .out(multiplexer_7_out), .sel(OPCODE_D3));  // open: in0, in12, in13, in14, in15, in16, in17, in18, in21, in23, in27, in28, in29, in30, in31
  Stack stack_1 (.Din(ALUOut), .W(Stack_W), .clk(clk), .R(Stack_R), .Dout(Dout_Stack));  // open: SPWritePTR, SPReadPTR
  not not_1 (not_1_out, Carry_Flag_D1);
  not not_2 (not_2_out, Zero_Flag_D1);
  Register_File register_file_1 (
    .clk(clk), .Datain(multiplexer_7_out), .AddressW(z_D3), .W(Reg_W), .R(Reg_R), .AddressR1(x),
    .AddressR2(y), .Rx(Rx), .Ry(Ry));
  not not_3 (not_3_out, Zero_Flag_D1);
  Multiplexer #(.select(3), .enable("false")) multiplexer_8 (
    .in0(T4_I1), .in1(T4_I2), .in2(T4_I3), .in3(T4_I4), .in4(T4_I0), .out(T4), .sel(out_12));  // open: in5, in6, in7
  Multiplexer #(.select(5), .disabled(0)) multiplexer_9 (
    .in0(1'b0), .in1(1'b0), .in2(1'b0), .in3(1'b0), .in4(1'b0), .in5(1'b0), .in6(1'b0), .in7(1'b0),
    .in8(1'b0), .in9(1'b0), .in10(1'b0), .in11(1'b0), .in12(1'b0), .in13(1'b1), .in14(Zero_Flag_D1),
    .in15(not_3_out), .in16(Carry_Flag_D1), .in17(not_1_out), .in18(1'b0), .in19(1'b0), .in20(1'b0),
    .in21(1'b0), .in22(1'b0), .in23(1'b0), .in24(1'b0), .in25(1'b0), .in26(1'b0), .in27(Zero_Flag_D1),
    .in28(not_2_out), .in29(1'b0), .in30(1'b0), .in31(1'b0), .out(UpdatePC), .sel(OPCODE_D3), .en(T4));
  Multiplexer #(.select(5), .width(8), .enable("false")) multiplexer_10 (
    .in0({8{1'b0}}), .in2(Rx), .in3(Rx), .in4(Rx), .in5(Rx), .in6(Rx), .in7(Rx), .in8(Rx), .in9(Rx),
    .in10({8{1'b0}}), .in11({8{1'b0}}), .in12(Rx), .in13(Rx), .in14({8{1'b0}}), .in15({8{1'b0}}),
    .in16({8{1'b0}}), .in17({8{1'b0}}), .in18({8{1'b0}}), .in19(Rx), .in20({8{1'b0}}), .in21({8{1'b0}}),
    .in22(Rx), .in23({8{1'b0}}), .in24({8{1'b0}}), .in25(Rx), .in26(Rx), .in27(Rx), .in28(PC_D2),
    .in29(PC_D2), .in30({8{1'b0}}), .in31({8{1'b0}}), .out(multiplexer_10_out), .sel(OPCODE_D1));  // open: in1
  Multiplexer #(.select(5), .width(8), .enable("false")) multiplexer_11 (
    .in11(Imm_D2), .in12(Imm_D2), .in22(Rx_D1), .in23(Rx_D1), .out(multiplexer_11_out), .sel(OPCODE_D2));  // open: in0, in1, in2, in3, in4, in5, in6, in7, in8, in9, in10, in13, in14, in15, in16, in17, in18, in19, in20, in21, in24, in25, in26, in27, in28, in29, in30, in31
  Multiplexer #(.select(5), .width(8), .enable("false")) multiplexer_12 (
    .in0({8{1'b0}}), .in1(Ry), .in2(Ry), .in3(Ry), .in4(Ry), .in5(Imm_D1), .in6(Imm_D1), .in7(Imm_D1),
    .in8(Imm_D1), .in9({8{1'b0}}), .in10(Imm_D1), .in11({8{1'b0}}), .in12({8{1'b0}}), .in13({8{1'b0}}),
    .in14({8{1'b0}}), .in15({8{1'b0}}), .in16({8{1'b0}}), .in17({8{1'b0}}), .in18({8{1'b0}}),
    .in19({8{1'b0}}), .in20({8{1'b0}}), .in21({8{1'b0}}), .in22({8{1'b0}}), .in23(Ry), .in24(Ry), .in25(Ry),
    .in26(Ry), .in27({1'b0, Imm_D1[6:0]}), .in28({1'b0, Imm_D1[6:0]}), .in29({8{1'b0}}), .in30({8{1'b0}}),
    .in31({8{1'b0}}), .out(multiplexer_12_out), .sel(OPCODE_D1));
  MUX32to1_1bit mux32to1_1bit_1 (.Inp32bit(32'h801000), .Sel(OPCODE_D2), .E(T3), .Out(SRAM_W));
  MUX32to1_1bit mux32to1_1bit_2 (.Inp32bit(32'h400800), .Sel(OPCODE_D2), .E(T3), .Out(SRAM_R));
  MUX32to1_1bit mux32to1_1bit_3 (.Inp32bit(32'h7e413fe), .Sel(out_7), .E(T1), .Out(Reg_R));
  MUX32to1_1bit mux32to1_1bit_4 (.Inp32bit(32'h7580ffe), .Sel(OPCODE_D3), .E(T4), .Out(Reg_W));
  MUX32to1_1bit mux32to1_1bit_5 (.Inp32bit(32'h200000), .Sel(OPCODE_D2), .E(T3), .Out(OUTPort_W));
  MUX32to1_1bit mux32to1_1bit_6 (.Inp32bit(32'h100000), .Sel(OPCODE_D2), .E(T3), .Out(INPort_R));
  ALU alu_1 (
    .Operand1(multiplexer_10_out), .Operand2(multiplexer_12_out), .CFlag_Save(C_Save), .clk(clk),
    .ALUOut(ALUOut), .CarryFlag(Carry_Flag), .ZeroFlag(Zero_Flag), .ALU_Save(ALU_Save), .OPCODE(OPCODE_D1),
    .ZFlag_Save(Z_Save), .ALUOut_D1(ALUOut_D1), .Imm7(Imm_D1[7]));
  DataMemorySRAM datamemorysram_1 (
    .Address(multiplexer_11_out), .Din(ALUOut), .W(SRAM_W), .clk(clk), .R(SRAM_R), .Dout(Dout_SRAM));
  MUX32to1_1bit mux32to1_1bit_7 (.Inp32bit(32'h1fa417fe), .Sel(OPCODE_D1), .E(T2), .Out(ALU_Save));
  MUX32to1_1bit mux32to1_1bit_8 (.Inp32bit(32'h70001fe), .Sel(OPCODE_D1), .E(T2), .Out(Z_Save));
  MUX32to1_1bit mux32to1_1bit_9 (.Inp32bit(32'h7000110), .Sel(OPCODE_D1), .E(T2), .Out(C_Save));
  MUX32to1_1bit mux32to1_1bit_10 (.Inp32bit(32'h40000), .Sel(OPCODE_D2), .E(T3), .Out(Stack_W));
  MUX32to1_1bit mux32to1_1bit_11 (.Inp32bit(32'h80000), .Sel(OPCODE_D2), .E(T3), .Out(Stack_R));
  Register #(.width(1)) register_2 (.D(Carry_Flag), .en(1'b1), .Q(Carry_Flag_D1), .clk(clk), .clr(1'b0));
  Register #(.width(1)) register_3 (.D(Zero_Flag), .en(1'b1), .Q(Zero_Flag_D1), .clk(clk), .clr(1'b0));
  Register register_4 (.D(Ry), .en(1'b1), .Q(Ry_D1), .clk(clk), .clr(1'b0));
  Register register_5 (.D(Rx), .en(1'b1), .Q(Rx_D1), .clk(clk), .clr(1'b0));
  Register #(.width(1)) register_6 (.D(Carry_Flag_D1), .en(1'b1), .Q(Carry_Flag_D2), .clk(clk), .clr(1'b0));
  Register #(.width(1)) register_7 (.D(Zero_Flag_D1), .en(1'b1), .Q(Zero_Flag_D2), .clk(clk), .clr(1'b0));
  Register register_8 (.D(Ry_D1), .en(1'b1), .Q(Ry_D2), .clk(clk), .clr(1'b0));
  Register register_9 (.D(Rx_D1), .en(1'b1), .Q(Rx_D2), .clk(clk), .clr(1'b0));

  // Other names for the same wires on the sheet: Leading_Instruction[2:0] = out_12; OPCODE[4:0] = out_7
endmodule

module DataMemorySRAM (
  input  [7:0] Address,
  input  [7:0] Din,
  input  W,
  input  clk,
  input  R,
  output [7:0] Dout
);

  wire [7:0] ram_1_data;

  RAM #(.bus("separate")) ram_1 (
    .addr(Address), .din(Din), .data(ram_1_data), .str(W), .sel(1'b1), .clk(clk), .ld(1'b1), .clr(1'b0));
  Register register_1 (.D(ram_1_data), .en(R), .Q(Dout), .clk(clk), .clr(1'b0));
endmodule

module Stack (
  input  [7:0] Din,
  input  W,
  input  clk,
  input  R,
  output [7:0] Dout,
  output [7:0] SPWritePTR,
  output [7:0] SPReadPTR
);

  wire or_1_out;
  wire [7:0] adder_1_out, multiplexer_1_out, multiplexer_2_out;

  Adder adder_1 (.a(SPWritePTR), .b(8'h1), .out(adder_1_out), .cin(1'b0));  // open: cout
  Subtractor subtractor_1 (.a(SPWritePTR), .b(8'h1), .out(SPReadPTR), .bin(1'b0));  // open: bout
  Multiplexer #(.select(2), .width(8), .disabled(0), .enable("false")) multiplexer_1 (
    .in0(SPWritePTR), .in1(adder_1_out), .in2(SPReadPTR), .out(multiplexer_1_out), .sel({R, W}));  // open: in3
  or or_1 (or_1_out, W, R);
  DataMemorySRAM datamemorysram_1 (.Address(multiplexer_2_out), .Din(Din), .W(W), .clk(clk), .R(R), .Dout(Dout));
  Register register_1 (.D(multiplexer_1_out), .en(or_1_out), .Q(SPWritePTR), .clk(clk), .clr(1'b0));
  Multiplexer #(.select(2), .width(8), .disabled(0), .enable("false")) multiplexer_2 (
    .in0({8{1'b0}}), .in1(SPWritePTR), .in2(SPReadPTR), .out(multiplexer_2_out), .sel({R, W}));  // open: in3
endmodule

module RegisterSynR (
  input  [7:0] Din,
  input  W,
  input  clk,
  output [7:0] Dout
);

  wire [7:0] register_1_q;

  Register register_1 (.D(Din), .en(W), .Q(register_1_q), .clk(clk), .clr(1'b0));
  Register register_2 (.D(register_1_q), .Q(Dout), .clk(clk), .clr(1'b0));  // open: en
endmodule

module ROM_SynR (
  input  [7:0] Address,
  input  clk,
  input  R,
  output [24:0] Inst,
  output [24:0] Inst_D1,
  output [24:0] Inst_D2,
  output [24:0] Inst_D3,
  output [7:0] Imm,
  output [3:0] Source2,
  output [7:0] Imm_D1,
  output [7:0] Imm_D2,
  output [7:0] Imm_D3,
  output [3:0] Source1,
  output [3:0] Dest,
  output [3:0] Source2_D1,
  output [3:0] Source2_D2,
  output [3:0] Source2_D3,
  output [4:0] OPCODE,
  output [3:0] Source1_D1,
  output [3:0] Source1_D2,
  output [3:0] Source1_D3,
  output [3:0] Dest_D1,
  output [3:0] Dest_D2,
  output [3:0] Dest_D3,
  output [4:0] OPCODE_D1,
  output [4:0] OPCODE_D2,
  output [4:0] OPCODE_D3
);

  wire [24:0] rom_1_data;

  ROM #(.dataWidth(25)) rom_1 (.addr(Address), .data(rom_1_data), .sel(1'b1));
  Register #(.width(25)) register_1 (
    .D(rom_1_data), .en(R), .Q({Inst[24:20], Dest, Inst[15:8], Imm}), .clk(clk), .clr(1'b0));
  Register #(.width(25)) register_2 (
    .D({Inst[24:20], Dest, Inst[15:8], Imm}), .en(1'b1),
    .Q({Inst_D1[24:20], Dest_D1, Inst_D1[15:8], Imm_D1}), .clk(clk), .clr(1'b0));
  Register #(.width(25)) register_3 (
    .D({Inst_D1[24:20], Dest_D1, Inst_D1[15:8], Imm_D1}), .en(1'b1),
    .Q({Inst_D2[24:20], Dest_D2, Inst_D2[15:8], Imm_D2}), .clk(clk), .clr(1'b0));
  Register #(.width(25)) register_4 (
    .D({Inst_D2[24:20], Dest_D2, Inst_D2[15:8], Imm_D2}), .en(1'b1),
    .Q({Inst_D3[24:20], Dest_D3, Inst_D3[15:8], Imm_D3}), .clk(clk), .clr(1'b0));

  assign {Inst[19:16], Inst[7:0]} = {Dest, Imm};
  assign {Inst_D1[19:16], Inst_D1[7:0]} = {Dest_D1, Imm_D1};
  assign {Inst_D2[19:16], Inst_D2[7:0]} = {Dest_D2, Imm_D2};
  assign {Inst_D3[19:16], Inst_D3[7:0]} = {Dest_D3, Imm_D3};
  assign OPCODE = Inst[24:20];
  assign OPCODE_D1 = Inst_D1[24:20];
  assign OPCODE_D2 = Inst_D2[24:20];
  assign OPCODE_D3 = Inst_D3[24:20];
  assign Source1 = Inst[15:12];
  assign Source1_D1 = Inst_D1[15:12];
  assign Source1_D2 = Inst_D2[15:12];
  assign Source1_D3 = Inst_D3[15:12];
  assign Source2 = Inst[11:8];
  assign Source2_D1 = Inst_D1[11:8];
  assign Source2_D2 = Inst_D2[11:8];
  assign Source2_D3 = Inst_D3[11:8];

  // Notes on the sheet:
  //   contents of rom_1 (hex, n*v repeats v):
  //   a10001 a20002 833003 844004 655005 0 0 0 c01031 c02032 c03033 c04034 c05035 5*0 d00000
endmodule

module ALU (
  input  Imm7,
  input  [7:0] Operand1,
  input  [7:0] Operand2,
  input  [4:0] OPCODE,
  input  ALU_Save,
  input  CFlag_Save,
  input  ZFlag_Save,
  input  clk,
  output [7:0] ALUOut,
  output [7:0] ALUOut_D1,
  output CarryFlag,
  output ZeroFlag
);

  wire Cout, multiplexer_3_out, nor_1_out;
  wire [7:0] ANDAnswer, ExORAnswer, LShiftAnswer, multiplexer_2_out, ORAnswer, RShiftAnswer, SUM, xor_1_out;
  wire [7:7] multiplexer_1_out;

  assign xor_1_out = {8{multiplexer_1_out[7]}} ^ Operand2;  // XOR_Gate xor_1, 8 bits wide
  Multiplexer #(.select(5), .enable("false")) multiplexer_1 (
    .in0(1'b0), .in1(1'b0), .in2(1'b0), .in3(1'b0), .in4(1'b0), .in5(1'b0), .in6(1'b0), .in7(1'b0),
    .in8(1'b0), .in9(1'b0), .in10(1'b0), .in11(1'b0), .in12(1'b0), .in13(1'b0), .in14(1'b0), .in15(1'b0),
    .in16(1'b0), .in17(1'b0), .in18(1'b0), .in19(1'b0), .in20(1'b0), .in21(1'b0), .in22(1'b0), .in23(1'b0),
    .in24(1'b1), .in25(1'b0), .in26(1'b0), .in27(Imm7), .in28(Imm7), .in29(1'b0), .in30(1'b0), .in31(1'b0),
    .out(multiplexer_1_out[7]), .sel(OPCODE));
  Adder adder_1 (.a(Operand1), .b(xor_1_out), .out(SUM), .cin(multiplexer_1_out[7]), .cout(Cout));
  assign ANDAnswer = Operand1 & Operand2;  // AND_Gate and_1, 8 bits wide
  assign ORAnswer = Operand1 | Operand2;  // OR_Gate or_1, 8 bits wide
  assign ExORAnswer = Operand1 ^ Operand2;  // XOR_Gate xor_2, 8 bits wide
  Shifter shifter_1 (.in(Operand1), .\dist (Operand2[2:0]), .out(LShiftAnswer));
  Shifter #(.shift("lr")) shifter_2 (.in(Operand1), .\dist (Operand2[2:0]), .out(RShiftAnswer));
  Multiplexer #(.select(5), .width(8), .enable("false")) multiplexer_2 (
    .in0(SUM), .in1(ANDAnswer), .in2(ORAnswer), .in3(ExORAnswer), .in4(SUM), .in5(ANDAnswer), .in6(ORAnswer),
    .in7(ExORAnswer), .in8(SUM), .in9(SUM), .in10(SUM), .in11({8{1'b0}}), .in12(SUM), .in13({8{1'b0}}),
    .in14({8{1'b0}}), .in15({8{1'b0}}), .in16({8{1'b0}}), .in17({8{1'b0}}), .in18(SUM), .in19({8{1'b0}}),
    .in20({8{1'b0}}), .in21(SUM), .in22({8{1'b0}}), .in23(SUM), .in24(SUM), .in25(RShiftAnswer),
    .in26(LShiftAnswer), .in27(SUM), .in28(SUM), .in29({8{1'b0}}), .in30({8{1'b0}}), .in31({8{1'b0}}),
    .out(multiplexer_2_out), .sel(OPCODE));
  Multiplexer #(.select(5), .enable("false")) multiplexer_3 (
    .in0(1'b0), .in1(1'b0), .in2(1'b0), .in3(1'b0), .in4(Cout), .in5(1'b0), .in6(1'b0), .in7(1'b0),
    .in8(Cout), .in9(1'b0), .in10(1'b0), .in11(1'b0), .in12(1'b0), .in13(1'b0), .in14(1'b0), .in15(1'b0),
    .in16(1'b0), .in17(1'b0), .in18(1'b0), .in19(1'b0), .in20(1'b0), .in21(1'b0), .in22(1'b0), .in23(1'b0),
    .in24(Cout), .in25(Operand1[0]), .in26(Operand1[7]), .in27(1'b0), .in28(1'b0), .in29(1'b0), .in30(1'b0),
    .in31(1'b0), .out(multiplexer_3_out), .sel(OPCODE));
  nor nor_1 (nor_1_out, multiplexer_2_out[0], multiplexer_2_out[1], multiplexer_2_out[2], multiplexer_2_out[3], multiplexer_2_out[4], multiplexer_2_out[5], multiplexer_2_out[6], multiplexer_2_out[7]);
  Register register_1 (.D(multiplexer_2_out), .en(ALU_Save), .Q(ALUOut), .clk(clk), .clr(1'b0));
  Register #(.width(1)) register_2 (.D(multiplexer_3_out), .en(CFlag_Save), .Q(CarryFlag), .clk(clk), .clr(1'b0));
  Register #(.width(1)) register_3 (.D(nor_1_out), .en(ZFlag_Save), .Q(ZeroFlag), .clk(clk), .clr(1'b0));
  Register register_4 (.D(ALUOut), .en(1'b1), .Q(ALUOut_D1), .clk(clk), .clr(1'b0));

  // Other names for the same wires on the sheet: Rx0 = Operand1[0]; Rx7 = Operand1[7]

  // Notes on the sheet:
  //   This is M (which controls Adder/Subtractor)
endmodule

module Timing (
  input  clk,
  output T0,
  output T1,
  output T2,
  output T3,
  output T4
);

  wire [2:0] adder_1_out, multiplexer_1_out, register_1_q;

  Adder #(.width(3)) adder_1 (.a(register_1_q), .b(3'b001), .out(adder_1_out), .cin(1'b0));  // open: cout
  Multiplexer #(.width(3), .enable("false")) multiplexer_1 (
    .in0(adder_1_out), .in1(3'b000), .out(multiplexer_1_out), .sel(T4));
  Register #(.width(3)) register_1 (.D(multiplexer_1_out), .en(1'b1), .Q(register_1_q), .clk(clk), .clr(1'b0));
  Decoder #(.select(3), .enable("false")) decoder_1 (
    .out0(T0), .out1(T1), .out2(T2), .out3(T3), .out4(T4), .sel(register_1_q));  // open: out5, out6, out7
endmodule

module PC (
  input  EnablePC,
  input  clk,
  input  [7:0] NewCAddress,
  input  UpdatePC,
  output [7:0] PC,
  output [7:0] PC_D1,
  output [7:0] PC_D2
);

  wire [7:0] adder_1_out, multiplexer_1_out, multiplexer_2_out;

  Multiplexer #(.width(8), .enable("false")) multiplexer_1 (
    .in0({8{1'b0}}), .in1(8'h1), .out(multiplexer_1_out), .sel(EnablePC));
  Adder adder_1 (.a(PC), .b(multiplexer_1_out), .out(adder_1_out), .cin(1'b0));  // open: cout
  Multiplexer #(.width(8), .enable("false")) multiplexer_2 (
    .in0(adder_1_out), .in1(NewCAddress), .out(multiplexer_2_out), .sel(UpdatePC));
  Register register_1 (.D(multiplexer_2_out), .en(1'b1), .Q(PC), .clk(clk), .clr(1'b0));
  Register register_2 (.D(PC), .en(1'b1), .Q(PC_D1), .clk(clk), .clr(1'b0));
  Register register_3 (.D(PC_D1), .en(1'b1), .Q(PC_D2), .clk(clk), .clr(1'b0));
endmodule

module Register_File (
  input  clk,
  input  [7:0] Datain,
  input  [3:0] AddressR1,
  input  [3:0] AddressW,
  input  W,
  input  [3:0] AddressR2,
  input  R,
  output [7:0] Rx,
  output [7:0] Ry
);

  wire decoder_1_out0, decoder_1_out1, decoder_1_out2, decoder_1_out3, decoder_1_out4, decoder_1_out5,
       decoder_1_out6, decoder_1_out7, decoder_1_out8, decoder_1_out9, decoder_1_out10, decoder_1_out11,
       decoder_1_out12, decoder_1_out13, decoder_1_out14, decoder_1_out15;
  wire [7:0] D0, D1, D2, D3, D4, D5, D6, D7, D8, D9, D10, D11, D12, D13, D14, D15, multiplexer_1_out,
       multiplexer_2_out;

  Decoder #(.select(4), .disabled(0)) decoder_1 (
    .out0(decoder_1_out0), .out1(decoder_1_out1), .out2(decoder_1_out2), .out3(decoder_1_out3),
    .out4(decoder_1_out4), .out5(decoder_1_out5), .out6(decoder_1_out6), .out7(decoder_1_out7),
    .out8(decoder_1_out8), .out9(decoder_1_out9), .out10(decoder_1_out10), .out11(decoder_1_out11),
    .out12(decoder_1_out12), .out13(decoder_1_out13), .out14(decoder_1_out14), .out15(decoder_1_out15),
    .sel(AddressW), .en(W));
  RegisterSynR registersynr_1 (.Din(Datain), .W(decoder_1_out0), .clk(clk), .Dout(D0));
  RegisterSynR registersynr_2 (.Din(Datain), .W(decoder_1_out1), .clk(clk), .Dout(D1));
  RegisterSynR registersynr_3 (.Din(Datain), .W(decoder_1_out2), .clk(clk), .Dout(D2));
  RegisterSynR registersynr_4 (.Din(Datain), .W(decoder_1_out3), .clk(clk), .Dout(D3));
  RegisterSynR registersynr_5 (.Din(Datain), .W(decoder_1_out4), .clk(clk), .Dout(D4));
  RegisterSynR registersynr_6 (.Din(Datain), .W(decoder_1_out5), .clk(clk), .Dout(D5));
  RegisterSynR registersynr_7 (.Din(Datain), .W(decoder_1_out6), .clk(clk), .Dout(D6));
  RegisterSynR registersynr_8 (.Din(Datain), .W(decoder_1_out7), .clk(clk), .Dout(D7));
  RegisterSynR registersynr_9 (.Din(Datain), .W(decoder_1_out8), .clk(clk), .Dout(D8));
  RegisterSynR registersynr_10 (.Din(Datain), .W(decoder_1_out9), .clk(clk), .Dout(D9));
  RegisterSynR registersynr_11 (.Din(Datain), .W(decoder_1_out10), .clk(clk), .Dout(D10));
  RegisterSynR registersynr_12 (.Din(Datain), .W(decoder_1_out11), .clk(clk), .Dout(D11));
  RegisterSynR registersynr_13 (.Din(Datain), .W(decoder_1_out12), .clk(clk), .Dout(D12));
  RegisterSynR registersynr_14 (.Din(Datain), .W(decoder_1_out13), .clk(clk), .Dout(D13));
  RegisterSynR registersynr_15 (.Din(Datain), .W(decoder_1_out14), .clk(clk), .Dout(D14));
  RegisterSynR registersynr_16 (.Din(Datain), .W(decoder_1_out15), .clk(clk), .Dout(D15));
  Multiplexer #(.select(4), .width(8), .enable("false")) multiplexer_1 (
    .in0(D0), .in1(D1), .in2(D2), .in3(D3), .in4(D4), .in5(D5), .in6(D6), .in7(D7), .in8(D8), .in9(D9),
    .in10(D10), .in11(D11), .in12(D12), .in13(D13), .in14(D14), .in15(D15), .out(multiplexer_1_out),
    .sel(AddressR1));
  Multiplexer #(.select(4), .width(8), .enable("false")) multiplexer_2 (
    .in0(D0), .in1(D1), .in2(D2), .in3(D3), .in4(D4), .in5(D5), .in6(D6), .in7(D7), .in8(D8), .in9(D9),
    .in10(D10), .in11(D11), .in12(D12), .in13(D13), .in14(D14), .in15(D15), .out(multiplexer_2_out),
    .sel(AddressR2));
  Register register_1 (.D(multiplexer_1_out), .en(R), .Q(Rx), .clk(clk), .clr(1'b0));
  Register register_2 (.D(multiplexer_2_out), .en(R), .Q(Ry), .clk(clk), .clr(1'b0));
endmodule

module INPort (
  input  [7:0] DatacomingfromExternal1World,
  input  clk,
  input  [7:0] DatacomingfromExternal2World,
  input  [7:0] DatacomingfromExternal3World,
  input  R,
  input  [7:0] DatacomingfromExternal4World,
  input  [7:0] CurrentAddress,
  output [7:0] INPort1Dout,
  output [7:0] INPortDataout,
  output [7:0] INPort2Dout,
  output [7:0] INPort3Dout,
  output [7:0] INPort4Dout
);

  wire comparator_1_eq, comparator_2_eq, comparator_3_eq, comparator_4_eq;
  wire [1:0] priority_encoder_1_out;
  wire [7:0] multiplexer_1_out;

  Comparator #(.mode("unsigned")) comparator_1 (.a(CurrentAddress), .b(8'hf1), .eq(comparator_1_eq));  // open: gt, lt
  Comparator #(.mode("unsigned")) comparator_2 (.a(CurrentAddress), .b(8'hf2), .eq(comparator_2_eq));  // open: gt, lt
  Comparator #(.mode("unsigned")) comparator_3 (.a(CurrentAddress), .b(8'hf3), .eq(comparator_3_eq));  // open: gt, lt
  Comparator #(.mode("unsigned")) comparator_4 (.a(CurrentAddress), .b(8'hf4), .eq(comparator_4_eq));  // open: gt, lt
  RegisterSynR registersynr_1 (.Din(DatacomingfromExternal1World), .W(1'b1), .clk(clk), .Dout(INPort1Dout));
  RegisterSynR registersynr_2 (.Din(DatacomingfromExternal2World), .W(1'b1), .clk(clk), .Dout(INPort2Dout));
  RegisterSynR registersynr_3 (.Din(DatacomingfromExternal3World), .W(1'b1), .clk(clk), .Dout(INPort3Dout));
  RegisterSynR registersynr_4 (.Din(DatacomingfromExternal4World), .W(1'b1), .clk(clk), .Dout(INPort4Dout));
  Priority_Encoder #(.select(2)) priority_encoder_1 (
    .in0(comparator_1_eq), .in1(comparator_2_eq), .in2(comparator_3_eq), .in3(comparator_4_eq),
    .out(priority_encoder_1_out), .en_in(1'b1));  // open: gs, en_out
  Multiplexer #(.select(2), .width(8), .enable("false")) multiplexer_1 (
    .in0(INPort1Dout), .in1(INPort2Dout), .in2(INPort3Dout), .in3(INPort4Dout), .out(multiplexer_1_out),
    .sel(priority_encoder_1_out));
  Register register_1 (.D(multiplexer_1_out), .en(R), .Q(INPortDataout), .clk(clk), .clr(1'b1));
endmodule

module OUTPort (
  input  [7:0] DatainOUTPort,
  input  clk,
  input  W,
  input  [7:0] CurrentAddress,
  output [7:0] DatavisibletoExternal1World,
  output [7:0] DatavisibletoExternal2World,
  output [7:0] DatavisibletoExternal3World,
  output [7:0] DatavisibletoExternal4World
);

  wire and_1_out, and_2_out, and_3_out, and_4_out, comparator_1_eq, comparator_2_eq, comparator_3_eq,
       comparator_4_eq;

  Comparator #(.mode("unsigned")) comparator_1 (.a(CurrentAddress), .b(8'hf8), .eq(comparator_1_eq));  // open: gt, lt
  Comparator #(.mode("unsigned")) comparator_2 (.a(CurrentAddress), .b(8'hf9), .eq(comparator_2_eq));  // open: gt, lt
  Comparator #(.mode("unsigned")) comparator_3 (.a(CurrentAddress), .b(8'hfa), .eq(comparator_3_eq));  // open: gt, lt
  Comparator #(.mode("unsigned")) comparator_4 (.a(CurrentAddress), .b(8'hfb), .eq(comparator_4_eq));  // open: gt, lt
  and and_1 (and_1_out, W, comparator_1_eq);
  and and_2 (and_2_out, W, comparator_2_eq);
  and and_3 (and_3_out, W, comparator_3_eq);
  and and_4 (and_4_out, W, comparator_4_eq);
  Register register_1 (.D(DatainOUTPort), .en(and_1_out), .Q(DatavisibletoExternal1World), .clk(clk), .clr(1'b0));
  Register register_2 (.D(DatainOUTPort), .en(and_2_out), .Q(DatavisibletoExternal2World), .clk(clk), .clr(1'b0));
  Register register_3 (.D(DatainOUTPort), .en(and_3_out), .Q(DatavisibletoExternal3World), .clk(clk), .clr(1'b0));
  Register register_4 (.D(DatainOUTPort), .en(and_4_out), .Q(DatavisibletoExternal4World), .clk(clk), .clr(1'b0));
endmodule

module MUX32to1_1bit (
  input  [31:0] Inp32bit,
  input  [4:0] Sel,
  input  E,
  output Out
);

  Multiplexer #(.select(5), .disabled(0)) multiplexer_1 (
    .in0(Inp32bit[0]), .in1(Inp32bit[1]), .in2(Inp32bit[2]), .in3(Inp32bit[3]), .in4(Inp32bit[4]),
    .in5(Inp32bit[5]), .in6(Inp32bit[6]), .in7(Inp32bit[7]), .in8(Inp32bit[8]), .in9(Inp32bit[9]),
    .in10(Inp32bit[10]), .in11(Inp32bit[11]), .in12(Inp32bit[12]), .in13(Inp32bit[13]), .in14(Inp32bit[14]),
    .in15(Inp32bit[15]), .in16(Inp32bit[16]), .in17(Inp32bit[17]), .in18(Inp32bit[18]), .in19(Inp32bit[19]),
    .in20(Inp32bit[20]), .in21(Inp32bit[21]), .in22(Inp32bit[22]), .in23(Inp32bit[23]), .in24(Inp32bit[24]),
    .in25(Inp32bit[25]), .in26(Inp32bit[26]), .in27(Inp32bit[27]), .in28(Inp32bit[28]), .in29(Inp32bit[29]),
    .in30(Inp32bit[30]), .in31(Inp32bit[31]), .out(Out), .sel(Sel), .en(E));
endmodule
